// Logisim project 1bit.circ as structural Verilog
module onebitadder (
  input  A,
  input  B,
  input  Cin,
  output S,
  output Cout
);

  wire and_1_out, and_2_out, xor_1_out;

  xor xor_1 (xor_1_out, A, B);
  xor xor_2 (S, xor_1_out, Cin);
  and and_1 (and_1_out, xor_1_out, Cin);
  and and_2 (and_2_out, A, B);
  or or_1 (Cout, and_1_out, and_2_out);
endmodule

module adder1 (
  input  [3:0] Ain,
  input  [3:0] Bin,
  input  cin,
  output out_4,
  output [3:0] out_5
);

  wire onebitadder_1_cout, onebitadder_2_cout, onebitadder_3_cout;

  onebitadder onebitadder_1 (.A(Ain[0]), .B(Bin[0]), .Cin(cin), .S(out_5[0]), .Cout(onebitadder_1_cout));
  onebitadder onebitadder_2 (.A(Ain[1]), .B(Bin[1]), .Cin(onebitadder_1_cout), .S(out_5[1]), .Cout(onebitadder_2_cout));
  onebitadder onebitadder_3 (.A(Ain[2]), .B(Bin[2]), .Cin(onebitadder_2_cout), .S(out_5[2]), .Cout(onebitadder_3_cout));
  onebitadder onebitadder_4 (.A(Ain[3]), .B(Bin[3]), .Cin(onebitadder_3_cout), .S(out_5[3]), .Cout(out_4));
endmodule
