// Logisim project ALU_template.circ as structural Verilog
module LeftShift32 (
  input  Cin,
  input  [31:0] B,
  input  [4:0] Sa,
  output [31:0] C
);

  wire [31:0] eightshift_1_zout, fourshifter_1_zout, multiplexer_1_out, multiplexer_2_out, multiplexer_3_out,
       multiplexer_4_out, onebitshifter_1_zout, sixtenshift_1_zout, twoshifter_1_zout;

  sixtenshift sixtenshift_1 (.cin(Cin), .sin(B), .zout(sixtenshift_1_zout));
  Multiplexer #(.width(32), .enable("false")) multiplexer_1 (
    .in0(B), .in1(sixtenshift_1_zout), .out(multiplexer_1_out), .sel(Sa[4]));
  eightshift eightshift_1 (.cin(Cin), .sin(multiplexer_1_out), .zout(eightshift_1_zout));
  Multiplexer #(.width(32), .enable("false")) multiplexer_2 (
    .in0(multiplexer_1_out), .in1(eightshift_1_zout), .out(multiplexer_2_out), .sel(Sa[3]));
  fourshifter fourshifter_1 (.Cin(Cin), .sin(multiplexer_2_out), .zout(fourshifter_1_zout));
  Multiplexer #(.width(32), .enable("false")) multiplexer_3 (
    .in0(multiplexer_2_out), .in1(fourshifter_1_zout), .out(multiplexer_3_out), .sel(Sa[2]));
  twoshifter twoshifter_1 (.cin(Cin), .Sin(multiplexer_3_out), .Zout(twoshifter_1_zout));
  Multiplexer #(.width(32), .enable("false")) multiplexer_4 (
    .in0(multiplexer_3_out), .in1(twoshifter_1_zout), .out(multiplexer_4_out), .sel(Sa[1]));
  oneBitShifter onebitshifter_1 (.Cin(Cin), .Sin(multiplexer_4_out), .zout(onebitshifter_1_zout));
  Multiplexer #(.width(32), .enable("false")) multiplexer_5 (
    .in0(multiplexer_4_out), .in1(onebitshifter_1_zout), .out(C), .sel(Sa[0]));
endmodule

module Add32 (
  input  [31:0] A,
  input  [31:0] B,
  input  Cin,
  output V,
  output [31:0] C
);

  wire add2_1_cout, add8_1_cout, adder4_1_cout, adder16_1_cout, onebitadder_1_cout, onebitadder_2_cout;

  adder16 adder16_1 (.A(A[15:0]), .B(B[15:0]), .Cin(Cin), .Cout(adder16_1_cout), .S(C[15:0]));
  add8 add8_1 (.A(A[23:16]), .B(B[23:16]), .Cin(adder16_1_cout), .Cout(add8_1_cout), .S(C[23:16]));
  adder4 adder4_1 (.A(A[27:24]), .B(B[27:24]), .C(add8_1_cout), .COut(adder4_1_cout), .S(C[27:24]));
  ADD2 add2_1 (.A(A[29:28]), .B(B[29:28]), .CIN(adder4_1_cout), .COUT(add2_1_cout), .S(C[29:28]));
  onebitadder onebitadder_1 (.A(A[30]), .B(B[30]), .Cin(add2_1_cout), .S(C[30]), .Cout(onebitadder_1_cout));
  onebitadder onebitadder_2 (.A(A[31]), .B(B[31]), .Cin(onebitadder_1_cout), .S(C[31]), .Cout(onebitadder_2_cout));
  xor xor_1 (V, onebitadder_2_cout, onebitadder_1_cout);
endmodule

module ALU32 (
  input  [31:0] A,
  input  [31:0] B,
  input  [3:0] Op,
  input  [4:0] Sa,
  output [31:0] C,
  output V
);

  wire addsub_1_v, and_1_out, and_2_out, and_3_out, not_1_out, not_2_out;
  wire [31:0] addsub_1_c, and_4_out, compare_1_c, eq32_1_c, multiplexer_1_out, multiplexer_2_out,
       multiplexer_3_out, multiplexer_4_out, multiplexer_5_out, multiplexer_6_out, multiplexer_7_out,
       multiplexer_8_out, nor_1_out, or_1_out, shiftsub_1_c, xor_1_out;

  and and_1 (and_1_out, Op[1], Op[2]);
  and and_2 (and_2_out, Op[0], Op[2]);
  not not_1 (not_1_out, Op[1]);
  and and_3 (and_3_out, Op[2], not_1_out);
  eq32 eq32_1 (.A(A), .B(B), .OP(Op[1]), .C(eq32_1_c));
  assign or_1_out = A | B;  // OR_Gate or_1, 32 bits wide
  assign and_4_out = A & B;  // AND_Gate and_4, 32 bits wide
  compare compare_1 (.A(A), .OP(and_1_out), .C(compare_1_c));
  assign nor_1_out = ~(A | B);  // NOR_Gate nor_1, 32 bits wide
  assign xor_1_out = A ^ B;  // XOR_Gate xor_1, 32 bits wide
  ADDSUB addsub_1 (.A(A), .B(B), .OP(and_3_out), .V(addsub_1_v), .C(addsub_1_c));
  Multiplexer #(.width(32), .enable("false")) multiplexer_1 (
    .in0(eq32_1_c), .in1(or_1_out), .out(multiplexer_1_out), .sel(Op[0]));
  Multiplexer #(.width(32), .enable("false")) multiplexer_2 (
    .in0(eq32_1_c), .in1(and_4_out), .out(multiplexer_2_out), .sel(Op[0]));
  SHIFTsub shiftsub_1 (.OpAr(and_2_out), .B(B), .SA(Sa), .OPL(Op[2]), .C(shiftsub_1_c));
  Multiplexer #(.width(32), .enable("false")) multiplexer_3 (
    .in0(compare_1_c), .in1(nor_1_out), .out(multiplexer_3_out), .sel(Op[0]));
  Multiplexer #(.width(32), .enable("false")) multiplexer_4 (
    .in0(compare_1_c), .in1(xor_1_out), .out(multiplexer_4_out), .sel(Op[0]));
  Multiplexer #(.width(32), .enable("false")) multiplexer_5 (
    .in0(addsub_1_c), .in1(shiftsub_1_c), .out(multiplexer_5_out), .sel(Op[1]));
  Multiplexer #(.width(32), .enable("false")) multiplexer_6 (
    .in0(multiplexer_1_out), .in1(multiplexer_2_out), .out(multiplexer_6_out), .sel(Op[1]));
  Multiplexer #(.width(32), .enable("false")) multiplexer_7 (
    .in0(multiplexer_3_out), .in1(multiplexer_4_out), .out(multiplexer_7_out), .sel(Op[1]));
  Multiplexer #(.width(32), .enable("false")) multiplexer_8 (
    .in0(multiplexer_6_out), .in1(multiplexer_7_out), .out(multiplexer_8_out), .sel(Op[2]));
  not not_2 (not_2_out, Op[1]);
  and and_5 (V, addsub_1_v, Op[3], not_2_out);
  Multiplexer #(.width(32), .enable("false")) multiplexer_9 (
    .in0(multiplexer_8_out), .in1(multiplexer_5_out), .out(C), .sel(Op[3]));
endmodule

module onebitadder (
  input  A,
  input  B,
  input  Cin,
  output S,
  output Cout
);

  wire and_1_out, and_2_out, xor_1_out;

  xor xor_1 (xor_1_out, A, B);
  xor xor_2 (S, xor_1_out, Cin);
  and and_1 (and_1_out, xor_1_out, Cin);
  and and_2 (and_2_out, A, B);
  or or_1 (Cout, and_1_out, and_2_out);
endmodule

module adder1 (
  input  [3:0] Ain,
  input  [3:0] Bin,
  input  cin,
  output out_4,
  output [3:0] out_5
);

  wire onebitadder_1_cout, onebitadder_2_cout, onebitadder_3_cout;

  onebitadder onebitadder_1 (.A(Ain[0]), .B(Bin[0]), .Cin(cin), .S(out_5[0]), .Cout(onebitadder_1_cout));
  onebitadder onebitadder_2 (.A(Ain[1]), .B(Bin[1]), .Cin(onebitadder_1_cout), .S(out_5[1]), .Cout(onebitadder_2_cout));
  onebitadder onebitadder_3 (.A(Ain[2]), .B(Bin[2]), .Cin(onebitadder_2_cout), .S(out_5[2]), .Cout(onebitadder_3_cout));
  onebitadder onebitadder_4 (.A(Ain[3]), .B(Bin[3]), .Cin(onebitadder_3_cout), .S(out_5[3]), .Cout(out_4));
endmodule

module adder16 (
  input  [15:0] A,
  input  [15:0] B,
  input  Cin,
  output Cout,
  output [15:0] S
);

  wire add8_1_cout;

  add8 add8_1 (.A(A[7:0]), .B(B[7:0]), .Cin(Cin), .Cout(add8_1_cout), .S(S[7:0]));
  add8 add8_2 (.A(A[15:8]), .B(B[15:8]), .Cin(add8_1_cout), .Cout(Cout), .S(S[15:8]));
endmodule

module add8 (
  input  [7:0] A,
  input  [7:0] B,
  input  Cin,
  output Cout,
  output [7:0] S
);

  wire adder4_1_cout;

  adder4 adder4_1 (.A(A[3:0]), .B(B[3:0]), .C(Cin), .COut(adder4_1_cout), .S(S[3:0]));
  adder4 adder4_2 (.A(A[7:4]), .B(B[7:4]), .C(adder4_1_cout), .COut(Cout), .S(S[7:4]));
endmodule

module adder4 (
  input  [3:0] A,
  input  [3:0] B,
  input  C,
  output COut,
  output [3:0] S
);

  wire onebitadder_1_cout, onebitadder_2_cout, onebitadder_3_cout;

  onebitadder onebitadder_1 (.A(A[0]), .B(B[0]), .Cin(C), .S(S[0]), .Cout(onebitadder_1_cout));
  onebitadder onebitadder_2 (.A(A[1]), .B(B[1]), .Cin(onebitadder_1_cout), .S(S[1]), .Cout(onebitadder_2_cout));
  onebitadder onebitadder_3 (.A(A[2]), .B(B[2]), .Cin(onebitadder_2_cout), .S(S[2]), .Cout(onebitadder_3_cout));
  onebitadder onebitadder_4 (.A(A[3]), .B(B[3]), .Cin(onebitadder_3_cout), .S(S[3]), .Cout(COut));
endmodule

module oneBitShifter (
  input  Cin,
  input  [31:0] Sin,
  output [31:0] zout
);


  assign zout = {Sin[30:0], Cin};
endmodule

module twoshifter (
  input  cin,
  input  [31:0] Sin,
  output [31:0] Zout
);

  wire [31:0] onebitshifter_1_zout;

  oneBitShifter onebitshifter_1 (.Cin(cin), .Sin(Sin), .zout(onebitshifter_1_zout));
  oneBitShifter onebitshifter_2 (.Cin(cin), .Sin(onebitshifter_1_zout), .zout(Zout));
endmodule

module fourshifter (
  input  Cin,
  input  [31:0] sin,
  output [31:0] zout
);

  wire [31:0] twoshifter_1_zout;

  twoshifter twoshifter_1 (.cin(Cin), .Sin(sin), .Zout(twoshifter_1_zout));
  twoshifter twoshifter_2 (.cin(Cin), .Sin(twoshifter_1_zout), .Zout(zout));
endmodule

module eightshift (
  input  cin,
  input  [31:0] sin,
  output [31:0] zout
);

  wire [31:0] fourshifter_1_zout;

  fourshifter fourshifter_1 (.Cin(cin), .sin(sin), .zout(fourshifter_1_zout));
  fourshifter fourshifter_2 (.Cin(cin), .sin(fourshifter_1_zout), .zout(zout));
endmodule

module sixtenshift (
  input  cin,
  input  [31:0] sin,
  output [31:0] zout
);

  wire [31:0] eightshift_1_zout;

  eightshift eightshift_1 (.cin(cin), .sin(sin), .zout(eightshift_1_zout));
  eightshift eightshift_2 (.cin(cin), .sin(eightshift_1_zout), .zout(zout));
endmodule

module ADD2 (
  input  [1:0] A,
  input  [1:0] B,
  input  CIN,
  output COUT,
  output [1:0] S
);

  wire onebitadder_1_cout;

  onebitadder onebitadder_1 (.A(A[0]), .B(B[0]), .Cin(CIN), .S(S[0]), .Cout(onebitadder_1_cout));
  onebitadder onebitadder_2 (.A(A[1]), .B(B[1]), .Cin(onebitadder_1_cout), .S(S[1]), .Cout(COUT));
endmodule

module ADDSUB (
  input  [31:0] A,
  input  [31:0] B,
  input  OP,
  output V,
  output [31:0] C
);

  wire [31:0] bit_extender_1_out, xor_1_out;

  assign bit_extender_1_out = {{31{OP}}, OP};  // Bit_Extender bit_extender_1
  assign xor_1_out = B ^ bit_extender_1_out;  // XOR_Gate xor_1, 32 bits wide
  sixtenshift sixtenshift_1 ();  // open: cin, sin, zout
  Add32 add32_1 (.A(A), .B(xor_1_out), .Cin(OP), .V(V), .C(C));
endmodule

module EQONEBIT (
  input  A,
  input  B,
  output C
);

  xnor xnor_1 (C, A, B);
endmodule

module SHIFTsub (
  input  OpAr,
  input  [31:0] B,
  input  [4:0] SA,
  input  OPL,
  output [31:0] C
);

  wire and_1_out;
  wire [31:0] leftshift32_1_c, multiplexer_1_out;

  and and_1 (and_1_out, B[31], OpAr);
  Multiplexer #(.width(32), .enable("false")) multiplexer_1 (
    .in0(B),
    .in1({B[0], B[1], B[2], B[3], B[4], B[5], B[6], B[7], B[8], B[9], B[10], B[11], B[12], B[13], B[14], B[15], B[16], B[17], B[18], B[19], B[20], B[21], B[22], B[23], B[24], B[25], B[26], B[27], B[28], B[29], B[30], B[31]}),
    .out(multiplexer_1_out), .sel(OPL));
  LeftShift32 leftshift32_1 (
    .Cin(and_1_out), .B(multiplexer_1_out), .Sa(SA),
    .C({leftshift32_1_c[0], leftshift32_1_c[1], leftshift32_1_c[2], leftshift32_1_c[3], leftshift32_1_c[4], leftshift32_1_c[5], leftshift32_1_c[6], leftshift32_1_c[7], leftshift32_1_c[8], leftshift32_1_c[9], leftshift32_1_c[10], leftshift32_1_c[11], leftshift32_1_c[12], leftshift32_1_c[13], leftshift32_1_c[14], leftshift32_1_c[15], leftshift32_1_c[16], leftshift32_1_c[17], leftshift32_1_c[18], leftshift32_1_c[19], leftshift32_1_c[20], leftshift32_1_c[21], leftshift32_1_c[22], leftshift32_1_c[23], leftshift32_1_c[24], leftshift32_1_c[25], leftshift32_1_c[26], leftshift32_1_c[27], leftshift32_1_c[28], leftshift32_1_c[29], leftshift32_1_c[30], leftshift32_1_c[31]}));
  Multiplexer #(.width(32), .enable("false")) multiplexer_2 (
    .in0({leftshift32_1_c[0], leftshift32_1_c[1], leftshift32_1_c[2], leftshift32_1_c[3], leftshift32_1_c[4], leftshift32_1_c[5], leftshift32_1_c[6], leftshift32_1_c[7], leftshift32_1_c[8], leftshift32_1_c[9], leftshift32_1_c[10], leftshift32_1_c[11], leftshift32_1_c[12], leftshift32_1_c[13], leftshift32_1_c[14], leftshift32_1_c[15], leftshift32_1_c[16], leftshift32_1_c[17], leftshift32_1_c[18], leftshift32_1_c[19], leftshift32_1_c[20], leftshift32_1_c[21], leftshift32_1_c[22], leftshift32_1_c[23], leftshift32_1_c[24], leftshift32_1_c[25], leftshift32_1_c[26], leftshift32_1_c[27], leftshift32_1_c[28], leftshift32_1_c[29], leftshift32_1_c[30], leftshift32_1_c[31]}),
    .in1(leftshift32_1_c), .out(C), .sel(OPL));
endmodule

module eqtwo (
  input  [1:0] A,
  input  [1:0] B,
  output [1:0] C
);

  wire and_1_out, eqonebit_1_c, eqonebit_2_c;

  EQONEBIT eqonebit_1 (.A(A[0]), .B(B[0]), .C(eqonebit_1_c));
  EQONEBIT eqonebit_2 (.A(A[1]), .B(B[1]), .C(eqonebit_2_c));
  and and_1 (and_1_out, eqonebit_1_c, eqonebit_2_c);
  assign C = {{1{1'b0}}, and_1_out};  // Bit_Extender bit_extender_1
endmodule

module eqfour (
  input  [3:0] A,
  input  [3:0] B,
  output [3:0] C
);

  wire [1:0] and_1_out, eqtwo_1_c, eqtwo_2_c;

  eqtwo eqtwo_1 (.A(A[1:0]), .B(B[1:0]), .C(eqtwo_1_c));
  eqtwo eqtwo_2 (.A(A[3:2]), .B(B[3:2]), .C(eqtwo_2_c));
  assign and_1_out = eqtwo_1_c & eqtwo_2_c;  // AND_Gate and_1, 2 bits wide
  assign C = {{2{1'b0}}, and_1_out};  // Bit_Extender bit_extender_1
endmodule

module eqEight (
  input  [7:0] A,
  input  [7:0] B,
  output [7:0] C
);

  wire [3:0] and_1_out, eqfour_1_c, eqfour_2_c;

  eqfour eqfour_1 (.A(A[3:0]), .B(B[3:0]), .C(eqfour_1_c));
  eqfour eqfour_2 (.A(A[7:4]), .B(B[7:4]), .C(eqfour_2_c));
  assign and_1_out = eqfour_1_c & eqfour_2_c;  // AND_Gate and_1, 4 bits wide
  assign C = {{4{1'b0}}, and_1_out};  // Bit_Extender bit_extender_1
endmodule

module edSixt (
  input  [15:0] A,
  input  [15:0] B,
  output [15:0] C
);

  wire [7:0] and_1_out, eqeight_1_c, eqeight_2_c;

  eqEight eqeight_1 (.A(A[7:0]), .B(B[7:0]), .C(eqeight_1_c));
  eqEight eqeight_2 (.A(A[15:8]), .B(B[15:8]), .C(eqeight_2_c));
  assign and_1_out = eqeight_1_c & eqeight_2_c;  // AND_Gate and_1, 8 bits wide
  assign C = {{8{1'b0}}, and_1_out};  // Bit_Extender bit_extender_1
endmodule

module eq32 (
  input  [31:0] A,
  input  [31:0] B,
  input  OP,
  output [31:0] C
);

  wire not_1_out, not_2_out, undriven, undriven_2, xor_1_out;
  wire [15:0] and_1_out, edsixt_1_c, edsixt_2_c;

  edSixt edsixt_1 (.A(A[15:0]), .B(B[15:0]), .C(edsixt_1_c));
  edSixt edsixt_2 (.A(A[31:16]), .B(B[31:16]), .C(edsixt_2_c));
  assign and_1_out = edsixt_1_c & edsixt_2_c;  // AND_Gate and_1, 16 bits wide
  not not_1 (not_1_out, OP);
  xor xor_1 (xor_1_out, not_1_out, and_1_out[0]);
  assign C = {{31{1'b0}}, xor_1_out};  // Bit_Extender bit_extender_1
  not not_2 (not_2_out, undriven);
  Multiplexer #(.enable("false")) multiplexer_1 (.in0(not_2_out), .sel(undriven_2));  // open: in1, out
endmodule

module compare (
  input  [31:0] A,
  input  OP,
  output [31:0] C
);

  wire and_1_out, xor_1_out, xor_2_out;

  and and_1 (and_1_out, ~A[0], ~A[1], ~A[2], ~A[3], ~A[4], ~A[5], ~A[6], ~A[7], ~A[8], ~A[9], ~A[10], ~A[11], ~A[12], ~A[13], ~A[14], ~A[15], ~A[16], ~A[17], ~A[18], ~A[19], ~A[20], ~A[21], ~A[22], ~A[23], ~A[24], ~A[25], ~A[26], ~A[27], ~A[28], ~A[29], ~A[30], ~A[31]);  // AND_Gate
  xor xor_1 (xor_1_out, and_1_out, A[31]);
  xor xor_2 (xor_2_out, xor_1_out, OP);
  assign C = {{31{1'b0}}, xor_2_out};  // Bit_Extender bit_extender_1
  Multiplexer #(.enable("false")) multiplexer_1 ();  // open: in0, in1, out, sel
endmodule

module CIRC1 (
  input  [31:0] A,
  input  [31:0] B,
  input  [3:0] OP,
  input  [4:0] in_4,
  output [31:0] C,
  output V
);

  wire and_1_out, and_2_out, not_1_out;
  wire [31:0] addsub_1_c, and_3_out, compare_1_c, eq32_1_c, multiplexer_1_out, multiplexer_2_out,
       multiplexer_3_out, multiplexer_4_out, multiplexer_5_out, multiplexer_6_out, multiplexer_7_out,
       multiplexer_8_out, nor_1_out, or_1_out, shiftsub_1_c, xor_1_out;

  and and_1 (and_1_out, OP[0], OP[2]);
  not not_1 (not_1_out, OP[1]);
  and and_2 (and_2_out, OP[2], not_1_out);
  eq32 eq32_1 (.A(A), .B(B), .OP(OP[1]), .C(eq32_1_c));
  assign or_1_out = A | B;  // OR_Gate or_1, 32 bits wide
  assign and_3_out = A & B;  // AND_Gate and_3, 32 bits wide
  compare compare_1 (.A(A), .OP(OP[2]), .C(compare_1_c));
  assign nor_1_out = ~(A | B);  // NOR_Gate nor_1, 32 bits wide
  assign xor_1_out = A ^ B;  // XOR_Gate xor_1, 32 bits wide
  ADDSUB addsub_1 (.A(A), .B(B), .OP(and_2_out), .V(V), .C(addsub_1_c));
  Multiplexer #(.width(32), .enable("false")) multiplexer_1 (
    .in0(eq32_1_c), .in1(or_1_out), .out(multiplexer_1_out), .sel(OP[0]));
  Multiplexer #(.width(32), .enable("false")) multiplexer_2 (
    .in0(eq32_1_c), .in1(and_3_out), .out(multiplexer_2_out), .sel(OP[0]));
  SHIFTsub shiftsub_1 (.OpAr(and_1_out), .B(B), .SA(in_4), .OPL(OP[2]), .C(shiftsub_1_c));
  Multiplexer #(.width(32), .enable("false")) multiplexer_3 (
    .in0(compare_1_c), .in1(nor_1_out), .out(multiplexer_3_out), .sel(OP[0]));
  Multiplexer #(.width(32), .enable("false")) multiplexer_4 (
    .in0(compare_1_c), .in1(xor_1_out), .out(multiplexer_4_out), .sel(OP[0]));
  Multiplexer #(.width(32), .enable("false")) multiplexer_5 (
    .in0(addsub_1_c), .in1(shiftsub_1_c), .out(multiplexer_5_out), .sel(OP[1]));
  Multiplexer #(.width(32), .enable("false")) multiplexer_6 (
    .in0(multiplexer_1_out), .in1(multiplexer_2_out), .out(multiplexer_6_out), .sel(OP[1]));
  Multiplexer #(.width(32), .enable("false")) multiplexer_7 (
    .in0(multiplexer_3_out), .in1(multiplexer_4_out), .out(multiplexer_7_out), .sel(OP[1]));
  Multiplexer #(.width(32), .enable("false")) multiplexer_8 (
    .in0(multiplexer_6_out), .in1(multiplexer_7_out), .out(multiplexer_8_out), .sel(OP[2]));
  Multiplexer #(.width(32), .enable("false")) multiplexer_9 (
    .in0(multiplexer_8_out), .in1(multiplexer_5_out), .out(C), .sel(OP[3]));
endmodule
