// Logisim project example.circ as structural Verilog: 1 circuit, main circuit main
module main (
  input  in_1,
  input  in_2,
  output out_3
);

  wire and_3_out, and_4_out, not_1_out, not_2_out;

  // AND_Gate and_1 is placed but not wired
  // AND_Gate and_2 is placed but not wired
  not not_1 (not_1_out, in_1);
  not not_2 (not_2_out, in_2);
  and and_3 (and_3_out, not_1_out, in_2);
  and and_4 (and_4_out, not_2_out, in_1);
  or or_1 (out_3, and_3_out, and_4_out);

  // Notes on the sheet:
  //   4-Bit Adder
  //   XOR CIRCUIT
endmodule
