// Logisim project fsm.circ as structural Verilog: 2 circuits, main circuit combLogic
module combLogic (
  input  S_0,
  input  S_1,
  input  inp,
  output C,
  output SN_0,
  output SN_1
);

  wire not_1_out;

  and and_1 (C, S_0, inp);
  not not_1 (not_1_out, inp);
  and and_2 (SN_0, S_1, not_1_out);

  assign SN_1 = inp;
endmodule

module overall (
  input  in_1,
  output out_2
);

  wire clock_1_out;
  wire [1:0] comblogic_1_sn_0, register_1_q;

  Clock clock_1 (.out(clock_1_out));
  Register #(.width(2)) register_1 (.D(comblogic_1_sn_0), .clk(clock_1_out), .Q(register_1_q));  // open: en, clr
  combLogic comblogic_1 (
    .S_0(register_1_q[0]), .S_1(register_1_q[1]), .inp(in_1), .C(out_2), .SN_0(comblogic_1_sn_0[0]),
    .SN_1(comblogic_1_sn_0[1]));
endmodule
