// Logisim project leftshift32_template.circ as structural Verilog: 6 circuits, main circuit LeftShift32
module LeftShift32 (
  input  Cin,
  input  [31:0] B,
  input  [4:0] Sa,
  output [31:0] C
);

  wire [31:0] eightshift_1_zout, fourshifter_1_zout, multiplexer_1_out, multiplexer_2_out, multiplexer_3_out,
       multiplexer_4_out, onebitshifter_1_zout, sixtenshift_1_zout, twoshifter_1_zout;

  Multiplexer #(.width(32), .enable("false")) multiplexer_1 (
    .in0(B), .in1(sixtenshift_1_zout), .out(multiplexer_1_out), .sel(Sa[4]));
  sixtenshift sixtenshift_1 (.cin(Cin), .sin(B), .zout(sixtenshift_1_zout));
  eightshift eightshift_1 (.cin(Cin), .sin(multiplexer_1_out), .zout(eightshift_1_zout));
  Multiplexer #(.width(32), .enable("false")) multiplexer_2 (
    .in0(multiplexer_1_out), .in1(eightshift_1_zout), .out(multiplexer_2_out), .sel(Sa[3]));
  fourshifter fourshifter_1 (.Cin(Cin), .sin(multiplexer_2_out), .zout(fourshifter_1_zout));
  Multiplexer #(.width(32), .enable("false")) multiplexer_3 (
    .in0(multiplexer_2_out), .in1(fourshifter_1_zout), .out(multiplexer_3_out), .sel(Sa[2]));
  twoshifter twoshifter_1 (.cin(Cin), .Sin(multiplexer_3_out), .Zout(twoshifter_1_zout));
  Multiplexer #(.width(32), .enable("false")) multiplexer_4 (
    .in0(multiplexer_3_out), .in1(twoshifter_1_zout), .out(multiplexer_4_out), .sel(Sa[1]));
  oneBitShifter onebitshifter_1 (.Cin(Cin), .Sin(multiplexer_4_out), .zout(onebitshifter_1_zout));
  Multiplexer #(.width(32), .enable("false")) multiplexer_5 (
    .in0(multiplexer_4_out), .in1(onebitshifter_1_zout), .out(C), .sel(Sa[0]));
endmodule

module oneBitShifter (
  input  Cin,
  input  [31:0] Sin,
  output [31:0] zout
);


  assign zout = {Sin[30:0], Cin};
endmodule

module twoshifter (
  input  cin,
  input  [31:0] Sin,
  output [31:0] Zout
);

  wire [31:0] onebitshifter_1_zout;

  oneBitShifter onebitshifter_1 (.Cin(cin), .Sin(Sin), .zout(onebitshifter_1_zout));
  oneBitShifter onebitshifter_2 (.Cin(cin), .Sin(onebitshifter_1_zout), .zout(Zout));
endmodule

module fourshifter (
  input  Cin,
  input  [31:0] sin,
  output [31:0] zout
);

  wire [31:0] twoshifter_1_zout;

  twoshifter twoshifter_1 (.cin(Cin), .Sin(sin), .Zout(twoshifter_1_zout));
  twoshifter twoshifter_2 (.cin(Cin), .Sin(twoshifter_1_zout), .Zout(zout));
endmodule

module eightshift (
  input  cin,
  input  [31:0] sin,
  output [31:0] zout
);

  wire [31:0] fourshifter_1_zout;

  fourshifter fourshifter_1 (.Cin(cin), .sin(sin), .zout(fourshifter_1_zout));
  fourshifter fourshifter_2 (.Cin(cin), .sin(fourshifter_1_zout), .zout(zout));
endmodule

module sixtenshift (
  input  cin,
  input  [31:0] sin,
  output [31:0] zout
);

  wire [31:0] eightshift_1_zout;

  eightshift eightshift_1 (.cin(cin), .sin(sin), .zout(eightshift_1_zout));
  eightshift eightshift_2 (.cin(cin), .sin(eightshift_1_zout), .zout(zout));
endmodule
